# Fritzing sketch MidiKick 2 (saved by Fritzing 0.9.4)
stripboards: 1

parts:
  Composant1 = Arduino Uno (Rev3)
  Display1 = LCD screen 16x2 IIC [part_number=101290]
  SET = SWITCH-MOMENTARY-2 [package=tactile-pth]
  PLUS = SWITCH-MOMENTARY-2 [package=tactile-pth]
  MINUS = SWITCH-MOMENTARY-2 [package=tactile-pth]
  MIDI_OUT = MIDI_CONN_FEMALE_SUPPORT [package=din_5_female_support]
  KICK_IN = 1/4 inch mono jack [package=audio-jack-6.5mm-panel-mount]
  R1 = Resistor [tolerance=±5% resistance=1M package=THT]
  D1 = Zener Diode [part_number=1N4732A breakdown_voltage=4.7V package="Melf DO-213 AB [SMD]"]
  R2 = Resistor [tolerance=±5% resistance=10k package="0805 [SMD]"]
  R3 = Resistor [tolerance=±5% resistance=33k package="0805 [SMD]"]
  C1 = Capacitor [package=cap-pth-small2]
  R4 = Resistor [tolerance=±5% resistance=1k package=THT]

nets:
  N1: Composant1.A0, R2.Pin_0, R3.Pin_0, C1.1
  N2: Composant1.A4/SDA, Display1.SDA
  N3: Composant1.A5/SCL, Display1.SCL
  GND: Composant1.GND, Display1.GND, SET.2, MINUS.2, KICK_IN.Tip, R1.Pin_0, D1.anode, C1.2
  N4: Composant1.D1/TX, MIDI_OUT.MIDI_IN
  N5: Composant1.D2, SET.1
  N6: Composant1.D3_PWM, MINUS.1
  N7: Composant1.D4, PLUS.1
  5V: Composant1.5V, Display1.VCC, R4.Pin_1
  N8: MIDI_OUT.MIDI_OUT, R4.Pin_0
  N9: KICK_IN.Sleeve, R1.Pin_1, D1.cathode, R2.Pin_1, R3.Pin_1

custom parts:
  LCD screen 16x2 IIC: LCD screen with HD44780 controller enables showing text, symbols, value or anything else that comes from Croduino/Arduino. It is capable of showing 16 symbols in two lines and therefore can be used in many projects that need to send clearly visible and legible output information.. • Color of symbols: White • Backlight: Blue • Dimensions: 80 x 36 x 12 mm • Screen dimensions: 64.5 x 16 mm •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
  1/4 inch mono jack: 1/4 inch mono Audio Jack Simple 1/4 inch panel mount audio jack.
